# Fritzing sketch Schematic (saved by Fritzing 0.9.4)

parts:
  L298N1 = L298N DC motor driver
  M2 = DC Motor  # not connected
  L298N2 = L298N DC motor driver
  M3 = DC Motor  # not connected
  M4 = DC Motor  # not connected
  M5 = DC Motor  # not connected
  Part1 = Arduino Uno (Rev3) - ICSP
  Part2 = RFID-RC522-v2
  Part3 = Bluetooth HC-05 Macho
  M6 = fc-51 [package=THT]
  M7 = fc-51 [package=THT]
  M8 = fc-51 [package=THT]
  M9 = fc-51 [package=THT]
  M10 = fc-51 [package=THT]

nets:
  N1: L298N1.ENB, Part1.D3_PWM
  N2: L298N1.IN3, Part1.D4
  N3: L298N1.IN4, Part1.D2
  N4: L298N2.5V, L298N2.ENA, Part1.D5_PWM
  N5: L298N2.IN2, Part1.D7
  N6: L298N2.IN4, Part1.D6_PWM
  N7: Part1.A0, M9.pin1
  N8: Part1.A1, M7.pin1
  N9: Part1.A2, M8.pin1
  N10: Part1.A3, M6.pin1
  N11: Part1.A4/SDA, M10.pin1
  N12: Part1.ICSP_MISO, Part1.D12/MISO, Part2.MISO
  N13: Part1.D9_PWM, Part2.RST
  N14: Part1.D10_PWM/SS, Part2.SDA
  N15: Part1.D11_PWM/MOSI, Part2.MOSI
  N16: Part1.D13/SCK, Part2.SCK
  GND: Part1.GND, Part2.GND
  N17: Part1.D0/RX, Part3.TXD
  N18: Part1.D1/TX, Part3.RXD

notes:
  Right From front
  Yellow is - (Black)
  Green is + (Red)
  Left From front
  Yellow is - (White)
  Green is + (Red)

custom parts:
  L298N DC motor driver: 2x DC motor driver with 78M05 positive voltage regulator (7..35 V) L298N: max 46 V, 2 A Set 5 V Enable jumper to enable 5 V regultor (needed for the L298N) and +5 V output at screw terminal or supply external +5 V at screw terminal Set ENA and/or ENB to +5 V to enable motor permanently or supply ENA and/or ENB with PWM signal IN1 and IN2 set rotation directory for motor A (OUT1/OUT2) IN2 and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
  RFID-RC522-v2: A simple China made RFID-RC522 Reader; do check the pin labels, as this is a MFRC522 based clone.
